# Fritzing sketch Nano_4in_4outMOS-2021-r2 (saved by Fritzing 0.9.3b)
circuit board: 7.2cm x 7.2cm
breadboards: 1

parts:
  Q1 = Basic FET P-Channel [package="TO220 [THT]"]
  Q2 = Basic FET P-Channel [package="TO220 [THT]"]
  Q3 = Basic FET P-Channel [package="TO220 [THT]"]
  Q4 = Basic FET P-Channel [package="TO220 [THT]"]
  R4 = Resistor [tolerance=±5% resistance=220 package=THT]
  OUT4 = LED - 3mm [color="Red (633nm)" package="3 mm [THT]"]
  OUT3 = LED - 3mm [color="Red (633nm)" package="3 mm [THT]"]
  R3 = Resistor [tolerance=±5% resistance=220 package=THT]
  OUT2 = LED - 3mm [color="Red (633nm)" package="3 mm [THT]"]
  R2 = Resistor [tolerance=±5% resistance=220 package=THT]
  OUT1 = LED - 3mm [color="Red (633nm)" package="3 mm [THT]"]
  24V_-_GND = Screw terminal - 2 pins [package=THT]
  J1 = Screw terminal - 2 pins [package=THT]
  J2 = Screw terminal - 2 pins [package=THT]
  J3 = Screw terminal - 2 pins [package=THT]
  J4 = Screw terminal - 2 pins [package=THT]
  U1 = Voltage Regulator - 5V [package="TO220 [THT]"]
  T2 = female pin header, 3 pins [form="♀ (female)"]
  IN-opto2 = Screw terminal - 2 pins [package=THT]
  CPU = Arduino Nano (Rev3.0)
  R1 = Resistor [tolerance=±5% resistance=220 package=THT]
  U1_2 = TLP621 [package=THT]
  Rio1 = Resistor [tolerance=±5% resistance=1.5k package=THT]
  Rio2 = Resistor [tolerance=±5% resistance=1.5k package=THT]
  IN1 = LED - 3mm [color="Green (570nm)" package="3 mm [THT]"]
  C1 = Ceramic Capacitor [capacitance=100nF package="100 mil [THT, multilayer]"]
  C2 = Electrolytic Capacitor [capacitance=1µF package="100 mil [THT, electrolytic]"]
  IN2 = LED - 3mm [color="Green (570nm)" package="3 mm [THT]"]
  IN-opto1 = Screw terminal - 2 pins [package=THT]
  IN-TTL = screw terminal, 4 pins
  Ri1 = Resistor [tolerance=±5% resistance=220 package=THT]
  R8 = Resistor [tolerance=±5% resistance=220 package=THT]
  R10 = Resistor [tolerance=±5% resistance=220 package=THT]
  J6 = Screw terminal - 2 pins [package=THT]
  J7 = Screw terminal - 2 pins [package=THT]
  U2 = TLP621 [package=THT]
  T1 = female pin header, 3 pins [form="♀ (female)"]
  5v-GND = screw terminal, 4 pins
  D1 = Rectifier Diode [part_number=1N4001 package="300 mil [THT]"]
  Ri2 = Resistor [tolerance=±5% resistance=220 package=THT]
  R14 = Resistor [tolerance=±5% resistance=220 package=THT]
  Ri3 = Resistor [tolerance=±5% resistance=220 package=THT]
  Ri4 = Resistor [tolerance=±5% resistance=220 package=THT]
  R17 = Resistor [tolerance=±5% resistance=220 package=THT]
  Rpu1 = Resistor [tolerance=±5% resistance=22k package=THT]
  Rpu2 = Resistor [tolerance=±5% resistance=22k package=THT]

nets:
  N1: Q1.gate, OUT1.anode, CPU.D5
  N2: Q1.drain, Q3.drain, Q4.drain, 24V_-_GND.pin1, U1.input_voltage, C2.+, D1.cathode, D1.anode
  N3: Q1.source, J1.pin1
  N4: Q2.gate, OUT2.anode, CPU.D6
  N5: Q2.source, J2.pin1
  N6: Q3.gate, Q4.gate, OUT4.anode, OUT3.anode, CPU.D7, CPU.D8, CPU.D9, CPU.D10, CPU.D11/MOSI, J6.pin1, J6.pin2
  N7: Q3.source, J3.pin1
  N8: Q4.source, J4.pin1
  GND: R4.Pin_0, R3.Pin_0, R2.Pin_0, 24V_-_GND.pin2, J1.pin2, J2.pin2, J3.pin2, J4.pin2, U1.GND, T2.pin3, CPU.GND, R1.Pin_0, U1_2.Pin_3, C1.1, C2.-, R8.Pin_0, R10.Pin_0, U2.Pin_3, T1.pin3, 5v-GND.pin4, R14.Pin_0, R17.Pin_0
  N9: R4.Pin_1, OUT4.cathode
  N10: OUT3.cathode, R3.Pin_1
  N11: OUT2.cathode, R2.Pin_1
  N12: OUT1.cathode, R1.Pin_1
  5V: U1.output_voltage, T2.pin1, CPU.VIN, CPU.5V, C1.0, T1.pin1, 5v-GND.pin1, 5v-GND.pin3, Rpu1.Pin_1, Rpu2.Pin_1
  N13: T2.pin2, CPU.A7
  N14: IN-opto2.pin1, U2.Pin_2
  N15: IN-opto2.pin2, Rio2.Pin_0
  N16: CPU.D1/TX, J7.pin1
  N17: CPU.D0/RX, J7.pin2
  N18: CPU.D12/MISO, U2.Pin_4, Rpu2.Pin_0
  N19: CPU.A6, T1.pin2
  N20: CPU.A3, R14.Pin_1, Ri4.Pin_1
  N21: CPU.A2, Ri3.Pin_1, R17.Pin_1
  N22: CPU.A1, R10.Pin_1, Ri2.Pin_1
  N23: CPU.A0, Ri1.Pin_1, R8.Pin_1
  N24: CPU.D13/SCK, U1_2.Pin_4, Rpu1.Pin_0
  N25: U1_2.Pin_1, IN1.cathode
  N26: U1_2.Pin_2, Rio1.Pin_1, IN1.anode, IN-opto1.pin1
  N27: Rio1.Pin_0, IN-opto1.pin2
  N28: Rio2.Pin_1, IN2.anode
  N29: IN2.cathode, U2.Pin_1
  N30: IN-TTL.pin1, IN-TTL.pin2, Ri1.Pin_0, Ri2.Pin_0
  N31: IN-TTL.pin3, Ri3.Pin_0
  N32: IN-TTL.pin4, Ri4.Pin_0
