# Fritzing sketch Nano_4in_4outMOS-2021-r3 (saved by Fritzing 0.9.3b)
circuit board: 10cm x 8cm
breadboards: 1

parts:
  Q1 = Basic FET P-Channel [package="TO220 [THT]"]
  Q2 = Basic FET P-Channel [package="TO220 [THT]"]
  Q3 = Basic FET P-Channel [package="TO220 [THT]"]
  Q4 = Basic FET P-Channel [package="TO220 [THT]"]
  R4 = Resistor [tolerance=±5% resistance=220 package=THT]
  OUT4 = LED - 3mm [color="Red (633nm)" package="3 mm [THT]"]
  OUT3 = LED - 3mm [color="Red (633nm)" package="3 mm [THT]"]
  R3 = Resistor [tolerance=±5% resistance=220 package=THT]
  OUT2 = LED - 3mm [color="Red (633nm)" package="3 mm [THT]"]
  R2 = Resistor [tolerance=±5% resistance=220 package=THT]
  OUT1 = LED - 3mm [color="Red (633nm)" package="3 mm [THT]"]
  24V-GND = Screw terminal - 2 pins [package=THT]
  J1 = Screw terminal - 2 pins [package=THT]
  J2 = Screw terminal - 2 pins [package=THT]
  J3 = Screw terminal - 2 pins [package=THT]
  J4 = Screw terminal - 2 pins [package=THT]
  U1 = Voltage Regulator - 5V [package="TO220 [THT]"]
  T2 = female pin header, 3 pins [form="♀ (female)"]
  IN-opto2 = Screw terminal - 2 pins [package=THT]
  CPU = Arduino Nano (Rev3.0)
  R1 = Resistor [tolerance=±5% resistance=220 package=THT]
  U1_2 = TLP621 [package=THT]
  Rio1 = Resistor [tolerance=±5% resistance=1.5k package=THT]
  Rio2 = Resistor [tolerance=±5% resistance=1.5k package=THT]
  IN1 = LED - 3mm [color="Green (570nm)" package="3 mm [THT]"]
  C2 = Electrolytic Capacitor [capacitance=1µF package="100 mil [THT, electrolytic]"]
  IN2 = LED - 3mm [color="Green (570nm)" package="3 mm [THT]"]
  IN-opto1 = Screw terminal - 2 pins [package=THT]
  IN-TTL = screw terminal, 4 pins
  Ri1 = Resistor [tolerance=±5% resistance=220 package=THT]
  Ri5 = Resistor [tolerance=±5% resistance=220 package=THT]
  Ri6 = Resistor [tolerance=±5% resistance=220 package=THT]
  OUT-TTL = Screw terminal - 2 pins [package=THT]
  COM = Screw terminal - 2 pins [package=THT]
  U2 = TLP621 [package=THT]
  T1 = female pin header, 3 pins [form="♀ (female)"]
  D1 = Rectifier Diode [part_number=1N4001 package="300 mil [THT]"]
  Ri2 = Resistor [tolerance=±5% resistance=220 package=THT]
  Ri8 = Resistor [tolerance=±5% resistance=220 package=THT]
  Ri3 = Resistor [tolerance=±5% resistance=220 package=THT]
  Ri4 = Resistor [tolerance=±5% resistance=220 package=THT]
  Ri7 = Resistor [tolerance=±5% resistance=220 package=THT]
  Rpu1 = Resistor [tolerance=±5% resistance=22k package=THT]
  Rpu2 = Resistor [tolerance=±5% resistance=22k package=THT]
  5V-GND = Screw terminal - 2 pins [package=THT]
  C1 = Ceramic Capacitor [capacitance=100nF package="200 mil [THT, multilayer]"]

nets:
  N1: Q1.gate, OUT1.anode, CPU.D5
  24V: Q1.drain, Q3.drain, Q4.drain, 24V-GND.pin1, U1.input_voltage, C2.+, D1.cathode, D1.anode
  N2: Q1.source, J1.pin1
  N3: Q2.gate, OUT2.anode, CPU.D6
  N4: Q2.source, J2.pin1
  N5: Q3.gate, Q4.gate, OUT4.anode, OUT3.anode, CPU.D7, CPU.D8, CPU.D9, CPU.D10, CPU.D11/MOSI, OUT-TTL.pin1, OUT-TTL.pin2
  N6: Q3.source, J3.pin1
  N7: Q4.source, J4.pin1
  GND: R4.Pin_0, R3.Pin_0, R2.Pin_0, 24V-GND.pin2, J1.pin2, J2.pin2, J3.pin2, J4.pin2, U1.GND, T2.pin3, CPU.GND, R1.Pin_0, U1_2.Pin_3, C2.-, Ri5.Pin_0, Ri6.Pin_0, U2.Pin_3, T1.pin3, Ri8.Pin_0, Ri7.Pin_0, 5V-GND.pin2, C1.1
  N8: R4.Pin_1, OUT4.cathode
  N9: OUT3.cathode, R3.Pin_1
  N10: OUT2.cathode, R2.Pin_1
  N11: OUT1.cathode, R1.Pin_1
  5V: U1.output_voltage, CPU.VIN, CPU.5V, T1.pin1, Rpu1.Pin_1, Rpu2.Pin_1, 5V-GND.pin1, C1.0
  N12: T2.pin2, CPU.A7
  N13: IN-opto2.pin1, U2.Pin_2
  N14: IN-opto2.pin2, Rio2.Pin_0
  N15: CPU.D1/TX, COM.pin1
  N16: CPU.D0/RX, COM.pin2
  N17: CPU.D12/MISO, U2.Pin_4, Rpu2.Pin_0
  N18: CPU.A6, T1.pin2
  N19: CPU.A3, Ri8.Pin_1, Ri4.Pin_1
  N20: CPU.A2, Ri3.Pin_1, Ri7.Pin_1
  N21: CPU.A1, Ri6.Pin_1, Ri2.Pin_1
  N22: CPU.A0, Ri1.Pin_1, Ri5.Pin_1
  N23: CPU.D13/SCK, U1_2.Pin_4, Rpu1.Pin_0
  N24: U1_2.Pin_1, IN1.cathode
  N25: U1_2.Pin_2, Rio1.Pin_1, IN1.anode, IN-opto1.pin1
  N26: Rio1.Pin_0, IN-opto1.pin2
  N27: Rio2.Pin_1, IN2.anode
  N28: IN2.cathode, U2.Pin_1
  N29: IN-TTL.pin1, IN-TTL.pin2, Ri1.Pin_0, Ri2.Pin_0
  N30: IN-TTL.pin3, Ri3.Pin_0
  N31: IN-TTL.pin4, Ri4.Pin_0
