# Fritzing sketch Nano_4in_4outMOS-big-opto2 (saved by Fritzing 0.9.3b)
circuit board: 7.2cm x 7.2cm
breadboards: 1

parts:
  Q1 = Basic FET P-Channel [package="TO220 [THT]"]
  Q2 = Basic FET P-Channel [package="TO220 [THT]"]
  Q3 = Basic FET P-Channel [package="TO220 [THT]"]
  Q4 = Basic FET P-Channel [package="TO220 [THT]"]
  R4 = Resistor [tolerance=±5% resistance=220 package=THT]
  OUT4 = LED - 3mm [color="Red (633nm)" package="3 mm [THT]"]
  OUT3 = LED - 3mm [color="Red (633nm)" package="3 mm [THT]"]
  R3 = Resistor [tolerance=±5% resistance=220 package=THT]
  OUT2 = LED - 3mm [color="Red (633nm)" package="3 mm [THT]"]
  R2 = Resistor [tolerance=±5% resistance=220 package=THT]
  OUT1 = LED - 3mm [color="Red (633nm)" package="3 mm [THT]"]
  24V_-_GND = Screw terminal - 2 pins [package=THT]
  J1 = Screw terminal - 2 pins [package=THT]
  J2 = Screw terminal - 2 pins [package=THT]
  J3 = Screw terminal - 2 pins [package=THT]
  J4 = Screw terminal - 2 pins [package=THT]
  U1 = Voltage Regulator - 5V [package="TO220 [THT]"]
  trimmer = female pin header, 3 pins [form="♀ (female)"]
  IN-opto2 = Screw terminal - 2 pins [package=THT]
  CPU = Arduino Nano (Rev3.0)
  R1 = Resistor [tolerance=±5% resistance=220 package=THT]
  U2 = TLP621 [package=THT]
  R5 = Resistor [tolerance=±5% resistance=1.5k package=THT]
  U3 = TLP621 [package=THT]
  R6 = Resistor [tolerance=±5% resistance=1.5k package=THT]
  IN1 = LED - 3mm [color="Green (570nm)" package="3 mm [THT]"]
  C1 = Ceramic Capacitor [capacitance=100nF package="100 mil [THT, multilayer]"]
  C2 = Electrolytic Capacitor [capacitance=1µF package="100 mil [THT, electrolytic]"]
  IN2 = LED - 3mm [color="Green (570nm)" package="3 mm [THT]"]
  IN-analog = screw terminal, 4 pins
  IN-opto1 = Screw terminal - 2 pins [package=THT]
  IN-5v = screw terminal, 4 pins
  R7 = Resistor [tolerance=±5% resistance=220 package=THT]
  R8 = Resistor [tolerance=±5% resistance=220 package=THT]
  R9 = Resistor [tolerance=±5% resistance=220 package=THT]
  R10 = Resistor [tolerance=±5% resistance=220 package=THT]
  R11 = Resistor [tolerance=±5% resistance=220 package=THT]
  R12 = Resistor [tolerance=±5% resistance=220 package=THT]
  J5 = Screw terminal - 2 pins [package=THT]
  J6 = Screw terminal - 2 pins [package=THT]
  J7 = Screw terminal - 2 pins [package=THT]

nets:
  N1: Q1.gate, OUT1.anode, CPU.D5
  24V: Q1.drain, Q2.drain, Q3.drain, Q4.drain, 24V_-_GND.pin1, U1.input_voltage, C2.+
  N2: Q1.source, J1.pin1
  N3: Q2.gate, OUT2.anode, CPU.D6
  N4: Q2.source, J2.pin1
  N5: Q3.gate, OUT3.anode, CPU.D8
  N6: Q3.source, J3.pin1
  N7: Q4.gate, OUT4.anode, CPU.D9
  N8: Q4.source, J4.pin1
  GND: R4.Pin_0, R3.Pin_0, R2.Pin_0, 24V_-_GND.pin2, J1.pin2, J2.pin2, J3.pin2, J4.pin2, U1.GND, trimmer.pin3, CPU.GND, R1.Pin_0, U2.Pin_3, U3.Pin_3, C1.1, C2.-, IN-analog.pin4, R8.Pin_0, R10.Pin_0, R12.Pin_0, J5.pin2
  N9: R4.Pin_1, OUT4.cathode
  N10: OUT3.cathode, R3.Pin_1
  N11: OUT2.cathode, R2.Pin_1
  N12: OUT1.cathode, R1.Pin_1
  N13: U1.output_voltage, trimmer.pin1, CPU.VIN, C1.0, IN-5v.pin1
  N14: trimmer.pin2, CPU.A7
  N15: IN-opto2.pin1, U3.Pin_2, IN2.cathode
  N16: IN-opto2.pin2, R6.Pin_0
  N17: CPU.D1/TX, J7.pin1
  N18: CPU.D0/RX, J7.pin2
  N19: CPU.D2, R11.Pin_1, R12.Pin_1
  N20: CPU.D3, R9.Pin_1, R10.Pin_1
  N21: CPU.D4, R7.Pin_1, R8.Pin_1
  N22: CPU.D7, J5.pin1
  N23: CPU.D10, J6.pin2
  N24: CPU.D11/MOSI, J6.pin1
  N25: CPU.D12/MISO, U3.Pin_4
  N26: CPU.A2, IN-analog.pin3
  N27: CPU.A1, IN-analog.pin2
  N28: CPU.A0, IN-analog.pin1
  N29: CPU.D13/SCK, U2.Pin_4
  N30: U2.Pin_1, R5.Pin_1, IN1.anode
  N31: U2.Pin_2, IN1.cathode, IN-opto1.pin1
  N32: R5.Pin_0, IN-opto1.pin2
  N33: U3.Pin_1, R6.Pin_1, IN2.anode
  N34: IN-5v.pin2, R7.Pin_0
  N35: IN-5v.pin3, R9.Pin_0
  N36: IN-5v.pin4, R11.Pin_0
