# Fritzing sketch Nano_4in_4outMOS-big (saved by Fritzing 0.9.3b)
circuit board: 4.2cm x 7.2cm
breadboards: 1

parts:
  Q1 = Basic FET P-Channel [package="TO220 [THT]"]
  Q2 = Basic FET P-Channel [package="TO220 [THT]"]
  Q3 = Basic FET P-Channel [package="TO220 [THT]"]
  Q4 = Basic FET P-Channel [package="TO220 [THT]"]
  R4 = Resistor [tolerance=±5% resistance=220 package=THT]
  OUT4 = LED - 3mm [color="Red (633nm)" package="3 mm [THT]"]
  OUT3 = LED - 3mm [color="Red (633nm)" package="3 mm [THT]"]
  R3 = Resistor [tolerance=±5% resistance=220 package=THT]
  OUT2 = LED - 3mm [color="Red (633nm)" package="3 mm [THT]"]
  R2 = Resistor [tolerance=±5% resistance=220 package=THT]
  OUT1 = LED - 3mm [color="Red (633nm)" package="3 mm [THT]"]
  24V_-_GND = Screw terminal - 2 pins [package=THT]
  J1 = Screw terminal - 2 pins [package=THT]
  J2 = Screw terminal - 2 pins [package=THT]
  J3 = Screw terminal - 2 pins [package=THT]
  J4 = Screw terminal - 2 pins [package=THT]
  U1 = Voltage Regulator - 5V [package="TO220 [THT]"]
  J6 = Screw terminal - 2 pins [package=THT]
  J8 = Screw terminal - 2 pins [package=THT]
  J9 = Screw terminal - 2 pins [package=THT]
  trimmer = female pin header, 3 pins [form="♀ (female)"]
  J7 = Screw terminal - 2 pins [package=THT]
  CPU = Arduino Nano (Rev3.0)
  R1 = Resistor [tolerance=±5% resistance=220 package=THT]
  U2 = TLP621 [package=THT]
  R5 = Resistor [tolerance=±5% resistance=1.5k package=THT]
  U3 = TLP621 [package=THT]
  R6 = Resistor [tolerance=±5% resistance=1.5k package=THT]
  OUT5 = LED - 3mm [color="Orange (612nm)" package="3 mm [THT]"]

nets:
  N1: Q1.gate, OUT1.anode, CPU.D5
  N2: Q1.drain, Q2.drain, Q3.drain, Q4.drain, 24V_-_GND.pin1, U1.input_voltage
  N3: Q1.source, J1.pin1
  N4: Q2.gate, OUT2.anode, CPU.D6
  N5: Q2.source, J2.pin1
  N6: Q3.gate, OUT3.anode, CPU.D8
  N7: Q3.source, J3.pin1
  N8: Q4.gate, OUT4.anode, CPU.D9
  N9: Q4.source, J4.pin1
  GND: R4.Pin_0, R3.Pin_0, R2.Pin_0, 24V_-_GND.pin2, J1.pin2, J2.pin2, J3.pin2, J4.pin2, U1.GND, trimmer.pin3, CPU.GND, R1.Pin_0, U2.Pin_3, U3.Pin_3
  N10: R4.Pin_1, OUT4.cathode
  N11: OUT3.cathode, R3.Pin_1
  N12: OUT2.cathode, R2.Pin_1
  N13: OUT1.cathode, R1.Pin_1
  N14: U1.output_voltage, CPU.VIN
  N15: J6.pin1, U2.Pin_2, OUT5.cathode
  N16: J6.pin2, R5.Pin_0
  N17: J8.pin1, CPU.A2
  N18: J8.pin2, J9.pin2, trimmer.pin1
  N19: J9.pin1, CPU.A3
  N20: trimmer.pin2, CPU.A7
  N21: J7.pin1, CPU.A1, U3.Pin_2
  N22: J7.pin2, R6.Pin_0
  N23: CPU.D12/MISO, U3.Pin_4
  N24: CPU.D13/SCK, U2.Pin_4
  N25: U2.Pin_1, R5.Pin_1, OUT5.anode
  N26: U3.Pin_1, R6.Pin_1
