# Fritzing sketch Nano_4in_4outMOS (saved by Fritzing 0.9.3b)
circuit board: 5.72086cm x 4.76811cm
breadboards: 1

parts:
  CPU = Arduino Nano (Rev3.0)
  Q1 = Basic FET P-Channel [package="TO220 [THT]"]
  Q2 = Basic FET P-Channel [package="TO220 [THT]"]
  Q3 = Basic FET P-Channel [package="TO220 [THT]"]
  Q4 = Basic FET P-Channel [package="TO220 [THT]"]
  R4 = Resistor [tolerance=±5% resistance=220 package=THT]
  LED4 = LED - 3mm [color="Red (633nm)" package="3 mm [THT]"]
  LED3 = LED - 3mm [color="Red (633nm)" package="3 mm [THT]"]
  R3 = Resistor [tolerance=±5% resistance=220 package=THT]
  LED2 = LED - 3mm [color="Red (633nm)" package="3 mm [THT]"]
  R2 = Resistor [tolerance=±5% resistance=220 package=THT]
  LED1 = LED - 3mm [color="Red (633nm)" package="3 mm [THT]"]
  R1 = Resistor [tolerance=±5% resistance=220 package=THT]
  24V_-_GND = Screw terminal - 2 pins [package=THT]
  J1 = Screw terminal - 2 pins [package=THT]
  J2 = Screw terminal - 2 pins [package=THT]
  J3 = Screw terminal - 2 pins [package=THT]
  J4 = Screw terminal - 2 pins [package=THT]
  U1 = Voltage Regulator - 5V [package="TO220 [THT]"]
  J6 = Screw terminal - 2 pins [package=THT]
  J7 = Screw terminal - 2 pins [package=THT]
  J8 = Screw terminal - 2 pins [package=THT]
  J9 = Screw terminal - 2 pins [package=THT]
  trimmer = female pin header, 3 pins [form="♀ (female)"]

nets:
  GND: CPU.GND, R4.Pin_0, R3.Pin_0, R2.Pin_0, R1.Pin_0, 24V_-_GND.pin2, J1.pin2, J2.pin2, J3.pin2, J4.pin2, U1.GND, trimmer.pin3
  N1: CPU.D2, Q1.gate, LED1.anode
  N2: CPU.D3, Q2.gate, LED2.anode
  N3: CPU.D4, Q3.gate, LED3.anode
  N4: CPU.D5, Q4.gate, LED4.anode
  N5: CPU.D8, CPU.A3, J9.pin1
  N6: CPU.D9, CPU.A2, J8.pin1
  N7: CPU.D10, CPU.A1, J7.pin1
  N8: CPU.D11/MOSI, CPU.A0, J6.pin1
  N9: CPU.VIN, U1.output_voltage, J6.pin2, J7.pin2, J8.pin2, J9.pin2, trimmer.pin1
  N10: CPU.A7, trimmer.pin2
  N11: Q1.drain, Q2.drain, Q3.drain, Q4.drain, 24V_-_GND.pin1, U1.input_voltage
  N12: Q1.source, J1.pin1
  N13: Q2.source, J2.pin1
  N14: Q3.source, J3.pin1
  N15: Q4.source, J4.pin1
  N16: R4.Pin_1, LED4.cathode
  N17: LED3.cathode, R3.Pin_1
  N18: LED2.cathode, R2.Pin_1
  N19: LED1.cathode, R1.Pin_1
